# Fritzing sketch Conexion_NODO_HUMEDAD (saved by Fritzing 0.9.3b)
breadboards: 2

parts:
  Componente1 = Arduino Nano (Rev3.0)
  Componente2 = NRF24L01+ Breakout Board
  Componente3 = Soil Moisture Sensor
  R3 = Resistor [tolerance=±1% resistance=100 package=THT]
  R1 = Resistor [tolerance=±1% resistance=6.8k package=THT]
  U2 = LIPO-110mAh [package=lipo-110]
  R2 = Resistor [tolerance=±1% resistance=150 package=THT]
  D1 = Rectifier Diode [part_number=1N4001 package="300 mil [THT]"]
  U1 = RELAY [package=relay-g5q]

nets:
  GND: Componente1.GND, Componente2.GND, Componente3.GND, R1.Pin_0, U2.-, R2.Pin_0, D1.anode, U1.NO
  N1: Componente1.D3, Componente3.VCC
  N2: Componente1.D5, D1.cathode, U1.COIL2
  N3: Componente1.D9, Componente2.CE
  N4: Componente1.D10, Componente2.CS
  N5: Componente1.D11/MOSI, Componente2.MOSI
  N6: Componente1.D12/MISO, Componente2.MISO
  N7: Componente1.VIN, U2.+, U1.MAIN
  N8: Componente1.A1, R3.Pin_0, R1.Pin_1, R2.Pin_1
  N9: Componente1.A0, Componente3.SIG
  3V3: Componente1.3V3, Componente2.VCC
  N10: Componente1.D13/SCK, Componente2.SCK
  N11: R3.Pin_1, U1.NC

// code stored in the sketch: prueba_rf.ino

