# Fritzing sketch Conexion_rf (saved by Fritzing 0.9.3b)
breadboards: 1

parts:
  Componente1 = Arduino Nano (Rev3.0)
  Componente2 = NRF24L01+ Breakout Board

nets:
  GND: Componente1.GND, Componente2.GND
  N1: Componente1.D9, Componente2.CE
  N2: Componente1.D10, Componente2.CS
  N3: Componente1.D11/MOSI, Componente2.MOSI
  N4: Componente1.D12/MISO, Componente2.MISO
  3V3: Componente1.3V3, Componente2.VCC
  N5: Componente1.D13/SCK, Componente2.SCK

// code stored in the sketch: prueba_rf.ino

