# Fritzing sketch Conexión_Nodo_Central (saved by Fritzing 0.9.3b)
breadboards: 1

parts:
  R1 = Resistor [tolerance=±1% resistance=4.7k package=THT]
  J1 = RJ11 Jack [package=rj11-6]
  C1 = Capacitor [package=cap-pth-small2]
  Componente2 = Dragino LoRa Shield V1.4
  Componente3 = Arduino Uno (Rev3)  # not connected
  Componente4 = NRF24L01+ Breakout Board

nets:
  N1: R1.Pin_0, C1.1, Componente2.5V
  N2: R1.Pin_1, J1.4, Componente2.3
  GND: J1.3, C1.2, Componente2.GND, Componente4.GND
  N3: Componente2.13, Componente4.SCK
  N4: Componente2.12, Componente4.MISO
  N5: Componente2.11, Componente4.MOSI
  N6: Componente2.5, Componente4.CS
  N7: Componente2.4, Componente4.CE
  3V3: Componente2.3V3, Componente4.VCC

notes:
  Sensor Precipitación
  4
  3
