# Fritzing sketch Conexión_Pluviometro_capacitor (saved by Fritzing 0.9.3b)
breadboards: 1

parts:
  Componente1 = Arduino Uno (Rev3)
  R1 = Resistor [tolerance=±1% resistance=4.7k package=THT]
  J1 = RJ11 Jack [package=rj11-6]
  C1 = Capacitor [package=cap-pth-small2]

nets:
  N1: Componente1.D3_PWM, R1.Pin_1, J1.4
  N2: Componente1.5V, R1.Pin_0, C1.1
  N3: Componente1.GND, J1.3, C1.2

notes:
  Sensor Precipitación
  4
  3
