# Fritzing sketch conexion_pH (saved by Fritzing 0.9.3b)
breadboards: 1

parts:
  S1 = PH meter [package=THT]
  U1 = LCD-16X2 [package=lcd-8x2]
  Componente1 = Arduino Nano (Rev3.0)
  R1 = Rotary Potentiometer (Small) [maximum_resistance=100kΩ package=THT]
  U2 = LIPO-110mAh [package=lipo-110]
  Componente2 = NRF24L01+ Breakout Board
  C1 = Electrolytic Capacitor [capacitance=10μF package="0605 [SMD, electrolytic]"]
  R2 = Resistor [tolerance=±1% resistance=150 package=THT]
  R3 = Resistor [tolerance=±1% resistance=6.8k package=THT]
  R4 = Resistor [tolerance=±1% resistance=100 package=THT]

nets:
  N1: S1.pin1, Componente1.A0
  VDD: S1.pin2, U1.VDD, Componente1.5V, R1.leg1, Componente2.VCC, C1.+
  GND: S1.pin3, U1.VSS, U1.R_W, Componente1.GND, R1.leg2, U2.-, Componente2.GND, C1.-, R2.Pin_0, R3.Pin_0
  N2: U1.VO, R1.wiper
  N3: U1.RS, Componente1.D3
  N4: U1.E, Componente1.D4
  N5: U1.DB4, Componente1.D5
  N6: U1.DB5, Componente1.D6
  N7: U1.DB6, Componente1.D7
  N8: U1.DB7, Componente1.D8
  N9: Componente1.D9, Componente2.CE
  N10: Componente1.D10, Componente2.CS
  N11: Componente1.D11/MOSI, Componente2.MOSI
  N12: Componente1.D12/MISO, Componente2.MISO
  N13: Componente1.VIN, U2.+, R4.Pin_1
  N14: Componente1.A5, R2.Pin_1, R3.Pin_1, R4.Pin_0
  N15: Componente1.D13/SCK, Componente2.SCK
