# Fritzing sketch conexión_higrometro (saved by Fritzing 0.9.3b)
breadboards: 1

parts:
  Componente1 = Soil Moisture Sensor
  Componente2 = Arduino Nano (Rev3.0) (ICSP)

nets:
  N1: Componente1.SIG, Componente2.A0
  GND: Componente1.GND, Componente2.GND
  VCC: Componente1.VCC, Componente2.5V
